# Fritzing sketch Projet_ELEC (saved by Fritzing 0.9.6b)

parts:
  LCD1 = LCD screen
  Mod1 = Raspberry Pi 4B
  HC-SR04_Sensor_1 = HC-SR04 Ultrasonic Distance Sensor  # not connected
  MD1 = Maker Drive
  M2 = DC Motor
  VCC1 = 4 x AAA Battery Mount  # not connected
  Grove1 = Grove Light Sensor  # not connected
  Grove2 = Grove Light Sensor  # not connected
  Grove3 = Grove Light Sensor  # not connected
  LCM1602_IIC1 = LCM1602 IIC [part_number="LCM1602 IIC" chip_label="LCM1602 IIC" package="DIP (Dual Inline) [THT]"]
  M1 = DC Motor

nets:
  VSS: LCD1.VSS, LCM1602_IIC1.VSS
  VDD: LCD1.VDD, LCM1602_IIC1.VDD
  N1: LCD1.V0, LCM1602_IIC1.V0
  N2: LCD1.RS, LCM1602_IIC1.RS
  N3: LCD1.R/W, LCM1602_IIC1.RW
  N4: LCD1.E, LCM1602_IIC1.E
  N5: LCD1.DB0, LCM1602_IIC1.D0
  N6: LCD1.DB1, LCM1602_IIC1.D1
  N7: LCD1.DB2, LCM1602_IIC1.D2
  N8: LCD1.DB3, LCM1602_IIC1.D3
  N9: LCD1.DB4, LCM1602_IIC1.D4
  N10: LCD1.DB5, LCM1602_IIC1.D5
  N11: LCD1.DB6, LCM1602_IIC1.D6
  N12: LCD1.DB7, LCM1602_IIC1.D7
  N13: LCD1.LED+, LCM1602_IIC1.A
  N14: LCD1.LED-, LCM1602_IIC1.K
  5V: Mod1.5V, MD1.5V, LCM1602_IIC1.VCC
  N15: Mod1.GPIO2, LCM1602_IIC1.SDA
  N16: Mod1.GPIO3, LCM1602_IIC1.SCL
  GND: Mod1.GND, MD1.GND, LCM1602_IIC1.GND
  N17: Mod1.GPIO18, MD1.M1A_IO
  N18: Mod1.GPIO12, MD1.M1B_IO
  N19: Mod1.GPIO13, MD1.M2A_IO
  N20: Mod1.GPIO19, MD1.M2B_IO
  N21: MD1.M1A, M2.pin_2
  N22: MD1.M1B, M2.pin_1
  N23: MD1.M2A, M1.pin_1
  N24: MD1.M2B, M1.pin_2

custom parts:
  Maker Drive: Simplifying H-Bridge Motor Driver for Beginner.
  LCM1602 IIC: I2C-Module to use a 1602 or 2004 LCD on with the wire.h libory Serial LCD Modul
